# Fritzing sketch vidix za h most s uzv FINALNO (saved by Fritzing 0.8.7b)
breadboards: 2

parts:
  Part2 = VIDI-X
  R1 = Resistor [tolerance=±5% resistance=220 package=THT]
  R2 = Resistor [tolerance=±5% resistance=220 package=THT]
  C1 = Ceramic Capacitor [capacitance=100nF package="100 mil [THT, multilayer]"]
  Q2 = Basic FET P-Channel [package="TO220 [THT]"]
  M1 = DC Motor
  Part3 = SRF05 Ultrasonic Rangefinder
  Part4 = SRF05 Ultrasonic Rangefinder
  U1 = Optocoupler [package=THT]
  U2 = Optocoupler [package=THT]
  Q4 = Basic FET N-Channel [package="TO220 [THT]"]
  Q5 = Basic FET N-Channel [package="TO220 [THT]"]
  R3 = Resistor [tolerance=±5% resistance=10k package=THT]
  R4 = Resistor [tolerance=±5% resistance=10k package=THT]
  Q3 = Basic FET P-Channel [package="TO220 [THT]"]
  BAT1 = BC9VPC [package=bc9vpc]

nets:
  GND: Part2.GND, Part3.GND, Part4.GND, U1.Pin_2, U2.Pin_2
  N1: Part2.BTN_A, Part3.Trig
  N2: Part2.BTN_2, Part3.Echo
  N3: Part2.CS1, R1.Pin_0
  N4: Part2.SELECT, Part4.Echo
  N5: R1.Pin_1, U2.Pin_1
  N6: R2.Pin_0, U1.Pin_1
  N7: C1.0, U1.Pin_4, U2.Pin_4, Q4.source, Q5.source, BAT1.V+
  N8: C1.1, Q2.source, R3.Pin_0, R4.Pin_0, Q3.source, BAT1.V-
  N9: Q2.gate, U1.Pin_5, Q4.gate, R3.Pin_1
  N10: Q2.drain, M1.pin_1, Q4.drain
  N11: M1.pin_2, Q5.drain, Q3.drain
  VCC: Part3.VCC, Part4.VCC
  N12: U2.Pin_5, Q5.gate, R4.Pin_1, Q3.gate

custom parts:
  VIDI-X: VIDI-X mikroračunalo, odostraga, s GPIO25/26 pinovima
